# Fritzing sketch circuit_design (saved by Fritzing 0.9.3b)
breadboards: 1

parts:
  Raspberry_Pi_1 = Raspberry Pi 3 [part_number=RPI-3-V1.2]
  S1 = Pushbutton [package="[THT]"]
  S2 = Pushbutton [package="[THT]"]
  S3 = Pushbutton [package="[THT]"]
  S4 = Pushbutton [package="[THT]"]
  LED4 = LED - 5mm [color="Yellow (595nm)" package="5 mm [THT]"]
  LED8 = LED - 5mm [color="Red (660nm)" package="5 mm [THT]"]
  LED9 = LED - 5mm [color="Red (660nm)" package="5 mm [THT]"]
  LED10 = LED - 5mm [color="Yellow (595nm)" package="5 mm [THT]"]
  LED11 = LED - 5mm [color="Red (660nm)" package="5 mm [THT]"]
  LED12 = LED - 5mm [color="Yellow (574nm)" package="5 mm [THT]"]
  LED13 = LED - 5mm [color="Red (660nm)" package="5 mm [THT]"]
  LED14 = LED - 5mm [color="Yellow (595nm)" package="5 mm [THT]"]
  R1 = Resistor [tolerance=±5% resistance=220 package=THT]
  R2 = Resistor [tolerance=±5% resistance=10 package=THT]
  R3 = Resistor [tolerance=±5% resistance=10 package=THT]
  R4 = Resistor [tolerance=±5% resistance=10 package=THT]
  R5 = Resistor [tolerance=±5% resistance=220 package=THT]
  R6 = Resistor [tolerance=±5% resistance=220 package=THT]
  R7 = Resistor [tolerance=±5% resistance=220 package=THT]
  R8 = Resistor [tolerance=±5% resistance=220 package=THT]
  R9 = Resistor [tolerance=±5% resistance=220 package=THT]
  R10 = Resistor [tolerance=±5% resistance=220 package=THT]
  R11 = Resistor [tolerance=±5% resistance=220 package=THT]
  R12 = Resistor [tolerance=±5% resistance=220 package=THT]

nets (from the breadboard view):
  N1: Raspberry_Pi_1.3v3, S1.Pin_3, S1.Pin_4, S2.Pin_3, S2.Pin_4, S3.Pin_3, S3.Pin_4, S4.Pin_3, S4.Pin_4
  N2: Raspberry_Pi_1.GPIO17, S1.Pin_1, S1.Pin_2, R1.Pin_0
  N3: Raspberry_Pi_1.GPIO27, S2.Pin_1, S2.Pin_2, R2.Pin_0
  N4: Raspberry_Pi_1.GPIO22, S3.Pin_1, S3.Pin_2, R3.Pin_0
  N5: Raspberry_Pi_1.GPIO10, S4.Pin_1, S4.Pin_2, R4.Pin_0
  N6: Raspberry_Pi_1.GND, LED4.anode, LED8.anode, LED9.anode, LED10.anode, LED11.anode, LED12.anode, LED13.anode, LED14.anode, R1.Pin_1, R2.Pin_1, R3.Pin_1, R4.Pin_1
  N7: Raspberry_Pi_1.GPIO7, R12.Pin_0
  N8: Raspberry_Pi_1.GPIO8, R11.Pin_0
  N9: Raspberry_Pi_1.GPIO25, R10.Pin_0
  N10: Raspberry_Pi_1.GPIO24, R9.Pin_0
  N11: Raspberry_Pi_1.GPIO23, R7.Pin_0
  N12: Raspberry_Pi_1.GPIO18, R8.Pin_0
  N13: Raspberry_Pi_1.GPIO15, R6.Pin_0
  N14: Raspberry_Pi_1.GPIO14, R5.Pin_0
  N15: LED4.cathode, R11.Pin_1
  N16: LED8.cathode, R12.Pin_1
  N17: LED9.cathode, R10.Pin_1
  N18: LED10.cathode, R9.Pin_1
  N19: LED11.cathode, R7.Pin_1
  N20: LED12.cathode, R8.Pin_1
  N21: LED13.cathode, R6.Pin_1
  N22: LED14.cathode, R5.Pin_1
